# Fritzing sketch computer-switch (saved by Fritzing 0.9.4)
perfboards: 1

parts:
  Part1 = Arduino Micro (Rev3)
  U1 = Sharp PC817 [package=THT]  # not connected
  J1 = Dagu DGServo 9g header (male) [package=THT]  # not connected
  U2 = V_REG_LD1117VXX [package=78xxl]
  R1 = Resistor [tolerance=±5% resistance=220 package=THT]
  Part2 = NRF24L01+ Breakout Board
  C1 = Electrolytic Capacitor [capacitance=10µF voltage=50V package="100 mil [THT, electrolytic]"]
  C2 = Electrolytic Capacitor [capacitance=100nF voltage=50V package="100 mil [THT, electrolytic]"]  # not connected

nets:
  GND: Part1.GND, U2.GND, Part2.GND, C1.+
  N1: Part1.D2/SDA, Part2.CE
  N2: Part1.D3/SCL, Part2.CS
  N3: Part1.D4_PWM/A6, R1.Pin_1
  N4: Part1.SCK, Part2.SCK
  N5: Part1.MISO, Part2.MISO
  N6: Part1.5V, U2.IN
  N7: U2.OUT, Part2.VCC, C1.-
