# Fritzing sketch door-bell (saved by Fritzing 0.9.4)
perfboards: 1

parts:
  MCU1 = Raspberry Pi Zero  # not connected
  D1 = Rectifier Diode [package="Melf DO-213 AA [SMD]"]
  D2 = Rectifier Diode [package="Melf DO-213 AA [SMD]"]
  D3 = Rectifier Diode [package="Melf DO-213 AA [SMD]"]
  D4 = Rectifier Diode [package="Melf DO-213 AA [SMD]"]
  J1 = Screw terminal - 2 pins [package=THT]  # not connected
  C1 = Capacitor Polarized [package=cpol-radial-100uf-25v]  # not connected
  C3 = Ceramic Capacitor [capacitance=100nF package="100 mil [THT, multilayer]"]
  U1 = Voltage Regulator [package=to-220-alt]  # not connected

nets:
  N1: D1.cathode, D3.anode
  N2: D1.anode, D2.cathode, C3.0
  N3: D2.anode, D4.anode
  N4: D3.cathode, D4.cathode, C3.1
