# Fritzing sketch irrigation-station-sketch (saved by Fritzing 0.9.4)
perfboards: 1

parts:
  Part3 = Arduino Micro (Rev3)
  J2 = Dagu DGServo 9g header (male) [package=THT]
  U4 = V_REG_LD1117VXX [package=78xxl]
  Part4 = NRF24L01+ Breakout Board
  J4 = Dagu DGServo 9g header (male) [package=THT]
  J6 = Dagu DGServo 9g header (male) [package=THT]
  KY-2 = Keyes Relay [package=THT]
  KY-3 = Keyes Relay [package=THT]
  KY-4 = Keyes Relay [package=THT]
  KY-5 = Keyes Relay [package=THT]
  KY-6 = Keyes Relay [package=THT]
  J8 = Power Jack [package=power_jack_combo]
  J7 = Power Jack [package=power_jack_combo]  # not connected
  J10 = female pin header, 2 pins [form="♀ (female)"]
  J11 = female pin header, 2 pins [form="♀ (female)"]
  J12 = female pin header, 2 pins [form="♀ (female)"]  # not connected
  J13 = female pin header, 2 pins [form="♀ (female)"]  # not connected
  J14 = female pin header, 2 pins [form="♀ (female)"]  # not connected
  J15 = female pin header, 2 pins [form="♀ (female)"]  # not connected
  J16 = female pin header, 2 pins [form="♀ (female)"]
  J17 = female pin header, 2 pins [form="♀ (female)"]
  J20 = Screw terminal - 2 pins [package=THT]
  M1 = RioRand LM2596
  J23 = Screw terminal - 2 pins [package=THT]
  J24 = Screw terminal - 2 pins [package=THT]
  J25 = Screw terminal - 2 pins [package=THT]
  J26 = Screw terminal - 2 pins [package=THT]
  J28 = Screw terminal - 2 pins [package=THT]

nets:
  N1: Part3.MOSI, Part4.MOSI
  GND: Part3.GND, U4.GND, Part4.GND, J4.pulse, KY-5.ground, J8.GND, J11.pin1, J16.pin1, J20.pin1, M1.Pin_1, J23.pin1, J24.pin1, J25.pin1, J26.pin1, J28.pin1
  N2: Part3.D2/SDA, J10.pin1, J17.pin1
  N3: Part3.D3/SCL, J10.pin2, J17.pin2
  N4: Part3.D4_PWM/A6, Part4.CE
  N5: Part3.D5_PWM, Part4.CS
  N6: Part3.D8_PWM/A8, J4.Vcc, KY-5.signal
  N7: Part3.D9_PWM/A9, J4.gnd, KY-4.signal
  N8: Part3.D10_PWM/A10, J2.pulse, KY-3.signal
  N9: Part3.D11_PWM, J2.Vcc, KY-2.signal
  N10: Part3.D12_PWM/A11, J2.gnd, KY-6.signal
  N11: Part3.SCK, Part4.SCK
  N12: Part3.MISO, Part4.MISO
  VIN: Part3.VIN, J6.gnd, KY-5.power, J8.PWR, J20.pin2, M1.Pin_2
  N13: Part3.5V, U4.IN
  N14: U4.OUT, Part4.VCC
  N15: KY-2.NC, J24.pin2
  N16: KY-2.C, KY-3.C, KY-4.C, KY-5.C, KY-6.C, M1.Pin_3
  N17: KY-3.NC, J26.pin2
  N18: KY-4.NC, J25.pin2
  N19: KY-5.NC, J28.pin2
  N20: KY-6.NC, J23.pin2
  N21: J11.pin2, J16.pin2

custom parts:
  Keyes Relay: The Keyes 5V relay module is suitable for SCM development, home appliance control. It uses a 5V~12V TIL control signal which can control DC / AC signal.
