# Fritzing sketch outlet-circuit (saved by Fritzing 0.9.4)
perfboards: 1

parts:
  Part1 = Arduino Nano (Rev3.0)  # not connected
  D1 = Diode [package=diode-1n4001]  # not connected
  D3 = Diode [package=diode-1n4001]
  D4 = Diode [package=diode-1n4001]  # not connected
  J2 = Camdenboss CTB0158-4 [part_number=CTB0158-4 package=THT]
  D2 = Diode [package=diode-1n4001]
  LTR_1 = Monacor line transformer [part_number=LTR-110]
  C1 = Electrolytic Capacitor [capacitance=1pF voltage=50V package="1010 [SMD, electrolytic]"]  # not connected

nets:
  N1: D3.C, LTR_1.08
  N2: J2.pin2, LTR_1.05
  N3: J2.pin4, LTR_1.01
  N4: D2.C, LTR_1.07
