# Fritzing sketch repeater (saved by Fritzing 0.9.4)
perfboards: 1

parts:
  Part1 = Arduino Micro (Rev3)
  U2 = V_REG_LD1117VXX [package=78xxl]
  Part2 = NRF24L01+ Breakout Board
  C1 = Electrolytic Capacitor [capacitance=10µF voltage=50V package="100 mil [THT, electrolytic]"]
  C2 = Electrolytic Capacitor [capacitance=100nF voltage=50V package="100 mil [THT, electrolytic]"]

nets:
  N1: Part1.D2/SDA, Part2.CE
  N2: Part1.D3/SCL, Part2.CS
  N3: Part1.SCK, Part2.SCK
  N4: Part1.MISO, Part2.MISO
  GND: Part1.GND, U2.GND, Part2.GND
  N5: Part1.5V, U2.IN, C2.-
  N6: U2.OUT, Part2.VCC, C1.-, C2.+
